// Logisim project Trabalho2.circ as structural Verilog: 12 circuits, main circuit main
module main (
  input  Reset
);

  wire clock_1_out, conjunto_1_hit, not_1_out;
  wire [3:0] mem_principal_1_offset, multiplexer_1_out;
  wire [7:0] banco_de_enderecos_1_endereco;
  wire [31:0] conjunto_1_dados, mem_principal_1_dados;

  Clock clock_1 (.out(clock_1_out));
  Banco_de_enderecos banco_de_enderecos_1 (
    .Hit(conjunto_1_hit), .Store(conjunto_1_hit), .Dados_Cache(conjunto_1_dados), .Clock(clock_1_out),
    .Endereco(banco_de_enderecos_1_endereco));  // open: Load
  not not_1 (not_1_out, conjunto_1_hit);
  Mem_principal mem_principal_1 (
    .Miss(not_1_out), .Clock(clock_1_out), .Offset(mem_principal_1_offset), .Dados(mem_principal_1_dados));  // open: Endereco
  Multiplexer #(.width(4), .enable("false")) multiplexer_1 (
    .in0(banco_de_enderecos_1_endereco[3:0]), .in1(mem_principal_1_offset), .out(multiplexer_1_out),
    .sel(not_1_out));
  Conjunto conjunto_1 (
    .Tag_in(banco_de_enderecos_1_endereco[7:4]), .Offset(multiplexer_1_out), .Dadoss(mem_principal_1_dados),
    .LoadBlock(not_1_out), .Reset(Reset), .Clock(clock_1_out), .Validade(not_1_out),
    .Tag_endereco(banco_de_enderecos_1_endereco[7:4]), .Dados(conjunto_1_dados), .Hit(conjunto_1_hit));

  // Notes on the sheet:
  //   BANCO DE ENDEREÇOS
  //   MEMORIA PRINCIPAL
  //   CACHE
endmodule

module Banco_de_enderecos (
  input  Hit,
  input  Store,
  input  Load,
  input  [31:0] Dados_Cache,
  input  Clock,
  output [7:0] Endereco
);

  wire [5:0] adder_1_out, and_1_out, Contador_q;

  assign and_1_out = {{5{1'b0}}, Hit} & 6'b000001;  // AND_Gate and_1, 6 bits wide
  Adder #(.width(6)) adder_1 (.a(and_1_out), .b(Contador_q), .out(adder_1_out));  // open: cin, cout
  Register #(.width(6)) Contador (.D(adder_1_out), .Q(Contador_q), .clk(Clock));  // open: en, clr
  ROM #(.addrWidth(6)) rom_1 (.addr(Contador_q), .data(Endereco), .sel(1'b1));
  RAM #(.addrWidth(6), .dataWidth(32), .bus("separate")) ram_1 (
    .addr(Contador_q), .din(Dados_Cache), .str(Store), .sel(1'b1), .clk(Clock), .ld(Load));  // open: data, clr

  // Notes on the sheet:
  //   Store
  //   contents of rom_1 (hex, n*v repeats v):
  //   0 1 2 3 4 5 6 7 8 9 a b c d e f 12*0 78
  //   SE FOR HIT, VEM UM FIO DE 6 BITS DA CACHE EM UMA DAS ENTRADAS DESSA PORTA (nao vai ser um PINO e sim 6 fios)
  //   Se for HIT, envia os dados para cá. Entao aqui no botao vai ser um fio de verificacao se é HIT ou NAO
endmodule

module Conjunto (
  input  [3:0] Tag_in,
  input  [3:0] Offset,
  input  [31:0] Dadoss,
  input  LoadBlock,
  input  Reset,
  input  Clock,
  input  Validade,
  input  [3:0] Tag_endereco,
  output Hit,
  output [31:0] Dados
);

  wire and_5_out, and_6_out, and_7_out, and_8_out, and_9_out, and_10_out, and_11_out, and_12_out, and_13_out,
       and_14_out, and_15_out, and_16_out, comparator_1_eq, comparator_2_eq, comparator_3_eq,
       comparator_4_eq, decoder_1_out0, decoder_1_out1, decoder_1_out2, decoder_1_out3, linha_1_validade_2,
       linha_2_validade_2, linha_3_validade_2, linha_4_validade_2, not_1_out, not_2_out, not_3_out,
       not_4_out, or_2_out, or_3_out, or_4_out, or_5_out, or_6_out, or_7_out, or_8_out;
  wire [1:0] Random_out;
  wire [3:0] and_1_out, linha_1_tag_2, linha_2_tag_2, linha_3_tag_2, linha_4_tag_2;
  wire [31:0] linha_1_dados, linha_2_dados, linha_3_dados, linha_4_dados;

  Linha linha_1 (
    .Dados_mem(Dadoss), .Offset(Offset), .Enable(or_2_out), .Reset(Reset), .Clock(Clock),
    .Validade(Validade), .Tag(Tag_in), .Dados(linha_1_dados), .Validade_2(linha_1_validade_2),
    .Tag_2(linha_1_tag_2));
  Comparator #(.width(4)) comparator_1 (.a(linha_1_tag_2), .b(Tag_endereco), .eq(comparator_1_eq));  // open: gt, lt
  and and_1 (and_1_out[0], comparator_1_eq, linha_1_validade_2);
  Comparator #(.width(4)) comparator_2 (.a(linha_2_tag_2), .b(Tag_endereco), .eq(comparator_2_eq));  // open: gt, lt
  or or_1 (Hit, and_1_out[0], and_1_out[1], and_1_out[2], and_1_out[3]);
  Linha linha_2 (
    .Dados_mem(Dadoss), .Offset(Offset), .Enable(or_4_out), .Reset(Reset), .Clock(Clock),
    .Validade(Validade), .Tag(Tag_in), .Dados(linha_2_dados), .Validade_2(linha_2_validade_2),
    .Tag_2(linha_2_tag_2));
  and and_2 (and_1_out[1], comparator_2_eq, linha_2_validade_2);
  Linha linha_3 (
    .Dados_mem(Dadoss), .Offset(Offset), .Enable(or_5_out), .Reset(Reset), .Clock(Clock),
    .Validade(Validade), .Tag(Tag_in), .Dados(linha_3_dados), .Validade_2(linha_3_validade_2),
    .Tag_2(linha_3_tag_2));
  Comparator #(.width(4)) comparator_3 (.a(linha_3_tag_2), .b(Tag_endereco), .eq(comparator_3_eq));  // open: gt, lt
  and and_3 (and_1_out[2], comparator_3_eq, linha_3_validade_2);
  Multiplexer #(.select(4), .width(32), .enable("false")) multiplexer_1 (
    .in1(linha_1_dados), .in2(linha_2_dados), .in4(linha_3_dados), .in8(linha_4_dados), .out(Dados),
    .sel(and_1_out));  // open: in0, in3, in5, in6, in7, in9, in10, in11, in12, in13, in14, in15
  Linha linha_4 (
    .Dados_mem(Dadoss), .Offset(Offset), .Enable(or_7_out), .Reset(Reset), .Clock(Clock),
    .Validade(Validade), .Tag(Tag_in), .Dados(linha_4_dados), .Validade_2(linha_4_validade_2),
    .Tag_2(linha_4_tag_2));
  Comparator #(.width(4)) comparator_4 (.a(linha_4_tag_2), .b(Tag_endereco), .eq(comparator_4_eq));  // open: gt, lt
  and and_4 (and_1_out[3], comparator_4_eq, linha_4_validade_2);
  or or_2 (or_2_out, and_13_out, or_3_out);
  or or_3 (or_3_out, and_5_out, and_6_out);
  and and_5 (and_5_out, LoadBlock, not_1_out, not_3_out, not_2_out);
  not not_1 (not_1_out, linha_4_validade_2);
  not not_2 (not_2_out, linha_1_validade_2);
  not not_3 (not_3_out, linha_2_validade_2);
  or or_4 (or_4_out, and_14_out, and_7_out);
  and and_6 (and_6_out, LoadBlock, linha_2_validade_2, not_2_out, linha_3_validade_2, linha_4_validade_2);
  and and_7 (and_7_out, LoadBlock, not_3_out, linha_4_validade_2);
  or or_5 (or_5_out, and_15_out, or_6_out);
  or or_6 (or_6_out, and_8_out, and_9_out);
  and and_8 (and_8_out, LoadBlock, linha_2_validade_2, not_4_out, linha_4_validade_2);
  not not_4 (not_4_out, linha_3_validade_2);
  and and_9 (and_9_out, LoadBlock, linha_1_validade_2, not_1_out, not_3_out, not_4_out);
  or or_7 (or_7_out, and_16_out, or_8_out);
  or or_8 (or_8_out, and_10_out, and_11_out);
  and and_10 (and_10_out, LoadBlock, linha_2_validade_2, not_1_out);
  and and_11 (and_11_out, LoadBlock, linha_1_validade_2, linha_3_validade_2, not_1_out);
  and and_12 (and_12_out, linha_4_validade_2, linha_3_validade_2, linha_2_validade_2, linha_1_validade_2);
  Random #(.width(2)) Random (.clk(LoadBlock), .out(Random_out));  // open: next, clr
  Decoder #(.select(2), .enable("false")) decoder_1 (
    .out0(decoder_1_out0), .out1(decoder_1_out1), .out2(decoder_1_out2), .out3(decoder_1_out3),
    .sel(Random_out));
  and and_13 (and_13_out, decoder_1_out0, and_12_out);
  and and_14 (and_14_out, decoder_1_out1, and_12_out);
  and and_15 (and_15_out, decoder_1_out2, and_12_out);
  and and_16 (and_16_out, decoder_1_out3, and_12_out);

  // Notes on the sheet:
  //   Essa parte é para quando acontece miss
endmodule

module Linha (
  input  [31:0] Dados_mem,
  input  [3:0] Offset,
  input  Enable,
  input  Reset,
  input  Clock,
  input  Validade,
  input  [3:0] Tag,
  output [31:0] Dados,
  output Validade_2,
  output [3:0] Tag_2
);

  wire and_1_out, and_2_out, and_3_out, and_4_out, and_5_out, decoder_1_out0, decoder_1_out1, decoder_1_out2,
       decoder_1_out3, not_1_out;
  wire [31:0] via_1_dados_out, via_2_dados_out, via_3_dados_out, via_4_dados_out;

  Decoder #(.select(2), .enable("false")) decoder_1 (
    .out0(decoder_1_out0), .out1(decoder_1_out1), .out2(decoder_1_out2), .out3(decoder_1_out3),
    .sel(Offset[3:2]));
  and and_1 (and_1_out, decoder_1_out0, Enable);
  and and_2 (and_2_out, decoder_1_out1, Enable);
  and and_3 (and_3_out, decoder_1_out2, Enable);
  and and_4 (and_4_out, decoder_1_out3, Enable);
  and and_5 (and_5_out, Enable, not_1_out);
  Register #(.width(1)) register_1 (.D(Validade), .en(and_5_out), .Q(Validade_2), .clk(Clock), .clr(Reset));
  not not_1 (not_1_out, Validade_2);
  Register #(.width(4)) register_2 (.D(Tag), .en(Enable), .Q(Tag_2), .clk(Clock), .clr(Reset));
  Via via_1 (.Dados(Dados_mem), .Enable(and_1_out), .Reset(Reset), .Clock(Clock), .Dados_out(via_1_dados_out));
  Via via_2 (.Dados(Dados_mem), .Enable(and_2_out), .Reset(Reset), .Clock(Clock), .Dados_out(via_2_dados_out));
  Via via_3 (.Dados(Dados_mem), .Enable(and_3_out), .Reset(Reset), .Clock(Clock), .Dados_out(via_3_dados_out));
  Via via_4 (.Dados(Dados_mem), .Enable(and_4_out), .Reset(Reset), .Clock(Clock), .Dados_out(via_4_dados_out));
  Multiplexer #(.select(2), .width(32), .enable("false")) multiplexer_1 (
    .in0(via_1_dados_out), .in1(via_2_dados_out), .in2(via_3_dados_out), .in3(via_4_dados_out), .out(Dados),
    .sel(Offset[3:2]));
endmodule

module Via (
  input  [31:0] Dados,
  input  Enable,
  input  Reset,
  input  Clock,
  output [31:0] Dados_out
);

  Register register_1 (.D(Dados[7:0]), .en(Enable), .Q(Dados_out[7:0]), .clk(Clock), .clr(Reset));
  Register register_2 (.D(Dados[15:8]), .en(Enable), .Q(Dados_out[15:8]), .clk(Clock), .clr(Reset));
  Register register_3 (.D(Dados[23:16]), .en(Enable), .Q(Dados_out[23:16]), .clk(Clock), .clr(Reset));
  Register register_4 (.D(Dados[31:24]), .en(Enable), .Q(Dados_out[31:24]), .clk(Clock), .clr(Reset));

  // Notes on the sheet:
  //   Aqui seleciona qual byte esta indexando ou 
endmodule

module Mem_principal (
  input  [7:0] Endereco,
  input  Miss,
  input  Clock,
  output [3:0] Offset,
  output [31:0] Dados
);

  wire [1:0] counter_1_q;
  wire [3:0] adder_1_out, adder_2_out, adder_3_out;
  wire [31:0] ram_1_data, ram_2_data, ram_3_data, ram_4_data;

  Adder #(.width(4)) adder_1 (.a(Endereco[3:0]), .b(4'b0100), .out(adder_1_out));  // open: cin, cout
  Adder #(.width(4)) adder_2 (.a(adder_1_out), .b(4'b0100), .out(adder_2_out));  // open: cin, cout
  Adder #(.width(4)) adder_3 (.a(adder_2_out), .b(4'b0100), .out(adder_3_out));  // open: cin, cout
  Counter #(.width(2), .max('h3)) counter_1 (.count(Miss), .Q(counter_1_q), .clk(Clock));  // open: load, D, carry, clr
  RAM #(.addrWidth(4), .dataWidth(32)) ram_1 (
    .addr(Endereco[7:4]), .data(ram_1_data), .sel(Miss), .clk(Clock), .ld(Miss));  // open: clr
  RAM #(.addrWidth(4), .dataWidth(32)) ram_2 (
    .addr(Endereco[7:4]), .data(ram_2_data), .sel(Miss), .clk(Clock), .ld(Miss));  // open: clr
  RAM #(.addrWidth(4), .dataWidth(32)) ram_3 (
    .addr(Endereco[7:4]), .data(ram_3_data), .sel(Miss), .clk(Clock), .ld(Miss));  // open: clr
  RAM #(.addrWidth(4), .dataWidth(32)) ram_4 (
    .addr(Endereco[7:4]), .data(ram_4_data), .sel(Miss), .clk(Clock), .ld(Miss));  // open: clr
  Multiplexer #(.select(2), .width(32)) multiplexer_1 (
    .in0(ram_1_data), .in1(ram_2_data), .in2(ram_3_data), .in3(ram_4_data), .out(Dados), .sel(counter_1_q),
    .en(Miss));
  Multiplexer #(.select(2), .width(4)) multiplexer_2 (
    .in0(Endereco[3:0]), .in1(adder_1_out), .in2(adder_2_out), .in3(adder_3_out), .out(Offset),
    .sel(counter_1_q), .en(Miss));
endmodule

module Dec4_1 (
  input  [3:0] in_1,
  output out_2,
  output out_3,
  output out_4,
  output out_5,
  output out_6,
  output out_7,
  output out_8,
  output out_9,
  output out_10,
  output out_11,
  output out_12,
  output out_13,
  output out_14,
  output out_15,
  output out_16,
  output out_17
);

  wire decoder_1_out0, decoder_2_out0, not_1_out, not_2_out, not_3_out;
  wire [2:0] and_1_out, and_4_out;

  not not_1 (not_1_out, in_1[3]);
  not not_2 (not_2_out, in_1[3]);
  not not_3 (not_3_out, in_1[3]);
  and and_1 (and_1_out[0], not_1_out, in_1[0]);
  and and_2 (and_1_out[1], not_2_out, in_1[1]);
  and and_3 (and_1_out[2], not_3_out, in_1[2]);
  and and_4 (and_4_out[0], in_1[3], in_1[0]);
  and and_5 (and_4_out[1], in_1[3], in_1[1]);
  and and_6 (and_4_out[2], in_1[3], in_1[2]);
  Decoder #(.select(3), .enable("false")) decoder_1 (
    .out0(decoder_1_out0), .out1(out_3), .out2(out_4), .out3(out_5), .out4(out_6), .out5(out_7),
    .out6(out_8), .out7(out_9), .sel(and_1_out));
  Decoder #(.select(3), .enable("false")) decoder_2 (
    .out0(decoder_2_out0), .out1(out_11), .out2(out_12), .out3(out_13), .out4(out_14), .out5(out_15),
    .out6(out_16), .out7(out_17), .sel(and_4_out));
  and and_7 (out_2, not_1_out, decoder_1_out0);
  and and_8 (out_10, in_1[3], decoder_2_out0);
endmodule

module Linha_bloco (
  input  [7:0] Dados_in,
  input  [3:0] Offset,
  input  Enable,
  input  Reset,
  input  Clock,
  input  Validade,
  input  [27:0] Tag,
  output [7:0] Dados_out,
  output Validade_2,
  output [27:0] Tag_2
);

  wire and_1_out, and_2_out, and_3_out, and_4_out, and_5_out, and_6_out, and_7_out, and_8_out, and_9_out,
       and_10_out, and_11_out, and_12_out, and_13_out, and_14_out, and_15_out, and_16_out, and_17_out,
       and_18_out, dec4_1_1_out_2, dec4_1_1_out_3, dec4_1_1_out_4, dec4_1_1_out_5, dec4_1_1_out_6,
       dec4_1_1_out_7, dec4_1_1_out_8, dec4_1_1_out_9, dec4_1_1_out_10, dec4_1_1_out_11, dec4_1_1_out_12,
       dec4_1_1_out_13, dec4_1_1_out_14, dec4_1_1_out_15, dec4_1_1_out_16, dec4_1_1_out_17, not_1_out;
  wire [7:0] register_3_q, register_4_q, register_5_q, register_6_q, register_7_q, register_8_q,
       register_9_q, register_10_q, register_11_q, register_12_q, register_13_q, register_14_q,
       register_15_q, register_16_q, register_17_q, register_18_q;

  Dec4_1 dec4_1_1 (
    .in_1(Offset), .out_2(dec4_1_1_out_2), .out_3(dec4_1_1_out_3), .out_4(dec4_1_1_out_4),
    .out_5(dec4_1_1_out_5), .out_6(dec4_1_1_out_6), .out_7(dec4_1_1_out_7), .out_8(dec4_1_1_out_8),
    .out_9(dec4_1_1_out_9), .out_10(dec4_1_1_out_10), .out_11(dec4_1_1_out_11), .out_12(dec4_1_1_out_12),
    .out_13(dec4_1_1_out_13), .out_14(dec4_1_1_out_14), .out_15(dec4_1_1_out_15), .out_16(dec4_1_1_out_16),
    .out_17(dec4_1_1_out_17));
  and and_1 (and_1_out, Enable, not_1_out);
  and and_2 (and_2_out, Enable, not_1_out);
  and and_3 (and_3_out, dec4_1_1_out_2, Enable);
  and and_4 (and_4_out, dec4_1_1_out_3, Enable);
  and and_5 (and_5_out, dec4_1_1_out_4, Enable);
  and and_6 (and_6_out, dec4_1_1_out_5, Enable);
  and and_7 (and_7_out, dec4_1_1_out_6, Enable);
  and and_8 (and_8_out, dec4_1_1_out_7, Enable);
  and and_9 (and_9_out, dec4_1_1_out_8, Enable);
  and and_10 (and_10_out, dec4_1_1_out_9, Enable);
  and and_11 (and_11_out, dec4_1_1_out_10, Enable);
  and and_12 (and_12_out, dec4_1_1_out_11, Enable);
  and and_13 (and_13_out, dec4_1_1_out_12, Enable);
  and and_14 (and_14_out, dec4_1_1_out_13, Enable);
  and and_15 (and_15_out, dec4_1_1_out_14, Enable);
  and and_16 (and_16_out, dec4_1_1_out_15, Enable);
  and and_17 (and_17_out, dec4_1_1_out_16, Enable);
  and and_18 (and_18_out, dec4_1_1_out_17, Enable);
  Register #(.width(1)) register_1 (.D(Validade), .en(and_1_out), .Q(Validade_2), .clk(Clock), .clr(Reset));
  not not_1 (not_1_out, Validade_2);
  Register #(.width(28)) register_2 (.D(Tag), .en(and_2_out), .Q(Tag_2), .clk(Clock), .clr(Reset));
  Register register_3 (.D(Dados_in), .en(and_3_out), .Q(register_3_q), .clk(Clock), .clr(Reset));
  Register register_4 (.D(Dados_in), .en(and_4_out), .Q(register_4_q), .clk(Clock), .clr(Reset));
  Register register_5 (.D(Dados_in), .en(and_5_out), .Q(register_5_q), .clk(Clock), .clr(Reset));
  Register register_6 (.D(Dados_in), .en(and_6_out), .Q(register_6_q), .clk(Clock), .clr(Reset));
  Register register_7 (.D(Dados_in), .en(and_7_out), .Q(register_7_q), .clk(Clock), .clr(Reset));
  Register register_8 (.D(Dados_in), .en(and_8_out), .Q(register_8_q), .clk(Clock), .clr(Reset));
  Register register_9 (.D(Dados_in), .en(and_9_out), .Q(register_9_q), .clk(Clock), .clr(Reset));
  Register register_10 (.D(Dados_in), .en(and_10_out), .Q(register_10_q), .clk(Clock), .clr(Reset));
  Register register_11 (.D(Dados_in), .en(and_11_out), .Q(register_11_q), .clk(Clock), .clr(Reset));
  Register register_12 (.D(Dados_in), .en(and_12_out), .Q(register_12_q), .clk(Clock), .clr(Reset));
  Register register_13 (.D(Dados_in), .en(and_13_out), .Q(register_13_q), .clk(Clock), .clr(Reset));
  Register register_14 (.D(Dados_in), .en(and_14_out), .Q(register_14_q), .clk(Clock), .clr(Reset));
  Register register_15 (.D(Dados_in), .en(and_15_out), .Q(register_15_q), .clk(Clock), .clr(Reset));
  Register register_16 (.D(Dados_in), .en(and_16_out), .Q(register_16_q), .clk(Clock), .clr(Reset));
  Register register_17 (.D(Dados_in), .en(and_17_out), .Q(register_17_q), .clk(Clock), .clr(Reset));
  Register register_18 (.D(Dados_in), .en(and_18_out), .Q(register_18_q), .clk(Clock), .clr(Reset));
  Multiplexer #(.select(4), .width(8), .enable("false")) multiplexer_1 (
    .in0(register_3_q), .in1(register_4_q), .in2(register_5_q), .in3(register_6_q), .in4(register_7_q),
    .in5(register_8_q), .in6(register_9_q), .in7(register_10_q), .in8(register_11_q), .in9(register_12_q),
    .in10(register_13_q), .in11(register_14_q), .in12(register_15_q), .in13(register_16_q),
    .in14(register_17_q), .in15(register_18_q), .out(Dados_out), .sel(Offset));
endmodule

module Cache (
  input  [31:0] \Endereço 
);

  wire [21:0] conjunto_teste_1_tag_0, conjunto_teste_1_tag_1, conjunto_teste_1_tag_2, conjunto_teste_1_tag_3,
       conjunto_teste_2_tag_3;

  Conjunto_teste conjunto_teste_1 (
    .Tag_3(conjunto_teste_1_tag_3), .Tag_2(conjunto_teste_1_tag_2), .Tag_1(conjunto_teste_1_tag_1),
    .Tag_0(conjunto_teste_1_tag_0));  // open: Tag_in, Offset, LoadBlock, Reset, Clock, Validade, Dado_3, Valid_3, Dado_2, Valid_2, Dado_3_2, Valid_1, Dado_0, Valid_0
  Conjunto_teste conjunto_teste_2 (.Tag_3(conjunto_teste_2_tag_3));  // open: Tag_in, Offset, LoadBlock, Reset, Clock, Validade, Dado_3, Valid_3, Dado_2, Valid_2, Tag_2, Dado_3_2, Valid_1, Tag_1, Dado_0, Valid_0, Tag_0
  Conjunto_teste conjunto_teste_3 ();  // open: Tag_in, Offset, LoadBlock, Reset, Clock, Validade, Dado_3, Valid_3, Tag_3, Dado_2, Valid_2, Tag_2, Dado_3_2, Valid_1, Tag_1, Dado_0, Valid_0, Tag_0
  Conjunto_teste conjunto_teste_4 ();  // open: Tag_in, Offset, LoadBlock, Reset, Clock, Validade, Dado_3, Valid_3, Tag_3, Dado_2, Valid_2, Tag_2, Dado_3_2, Valid_1, Tag_1, Dado_0, Valid_0, Tag_0
  Conjunto_teste conjunto_teste_5 ();  // open: Tag_in, Offset, LoadBlock, Reset, Clock, Validade, Dado_3, Valid_3, Tag_3, Dado_2, Valid_2, Tag_2, Dado_3_2, Valid_1, Tag_1, Dado_0, Valid_0, Tag_0
  Conjunto_teste conjunto_teste_6 ();  // open: Tag_in, Offset, LoadBlock, Reset, Clock, Validade, Dado_3, Valid_3, Tag_3, Dado_2, Valid_2, Tag_2, Dado_3_2, Valid_1, Tag_1, Dado_0, Valid_0, Tag_0
  Conjunto_teste conjunto_teste_7 ();  // open: Tag_in, Offset, LoadBlock, Reset, Clock, Validade, Dado_3, Valid_3, Tag_3, Dado_2, Valid_2, Tag_2, Dado_3_2, Valid_1, Tag_1, Dado_0, Valid_0, Tag_0
  Conjunto_teste conjunto_teste_8 ();  // open: Tag_in, Offset, LoadBlock, Reset, Clock, Validade, Dado_3, Valid_3, Tag_3, Dado_2, Valid_2, Tag_2, Dado_3_2, Valid_1, Tag_1, Dado_0, Valid_0, Tag_0
  Conjunto_teste conjunto_teste_9 ();  // open: Tag_in, Offset, LoadBlock, Reset, Clock, Validade, Dado_3, Valid_3, Tag_3, Dado_2, Valid_2, Tag_2, Dado_3_2, Valid_1, Tag_1, Dado_0, Valid_0, Tag_0
  Conjunto_teste conjunto_teste_10 ();  // open: Tag_in, Offset, LoadBlock, Reset, Clock, Validade, Dado_3, Valid_3, Tag_3, Dado_2, Valid_2, Tag_2, Dado_3_2, Valid_1, Tag_1, Dado_0, Valid_0, Tag_0
  Conjunto_teste conjunto_teste_11 ();  // open: Tag_in, Offset, LoadBlock, Reset, Clock, Validade, Dado_3, Valid_3, Tag_3, Dado_2, Valid_2, Tag_2, Dado_3_2, Valid_1, Tag_1, Dado_0, Valid_0, Tag_0
  Conjunto_teste conjunto_teste_12 ();  // open: Tag_in, Offset, LoadBlock, Reset, Clock, Validade, Dado_3, Valid_3, Tag_3, Dado_2, Valid_2, Tag_2, Dado_3_2, Valid_1, Tag_1, Dado_0, Valid_0, Tag_0
  Conjunto_teste conjunto_teste_13 ();  // open: Tag_in, Offset, LoadBlock, Reset, Clock, Validade, Dado_3, Valid_3, Tag_3, Dado_2, Valid_2, Tag_2, Dado_3_2, Valid_1, Tag_1, Dado_0, Valid_0, Tag_0
  Conjunto_teste conjunto_teste_14 ();  // open: Tag_in, Offset, LoadBlock, Reset, Clock, Validade, Dado_3, Valid_3, Tag_3, Dado_2, Valid_2, Tag_2, Dado_3_2, Valid_1, Tag_1, Dado_0, Valid_0, Tag_0
  Conjunto_teste conjunto_teste_15 ();  // open: Tag_in, Offset, LoadBlock, Reset, Clock, Validade, Dado_3, Valid_3, Tag_3, Dado_2, Valid_2, Tag_2, Dado_3_2, Valid_1, Tag_1, Dado_0, Valid_0, Tag_0
  Conjunto_teste conjunto_teste_16 ();  // open: Tag_in, Offset, LoadBlock, Reset, Clock, Validade, Dado_3, Valid_3, Tag_3, Dado_2, Valid_2, Tag_2, Dado_3_2, Valid_1, Tag_1, Dado_0, Valid_0, Tag_0
  Conjunto_teste conjunto_teste_17 ();  // open: Tag_in, Offset, LoadBlock, Reset, Clock, Validade, Dado_3, Valid_3, Tag_3, Dado_2, Valid_2, Tag_2, Dado_3_2, Valid_1, Tag_1, Dado_0, Valid_0, Tag_0
  Conjunto_teste conjunto_teste_18 ();  // open: Tag_in, Offset, LoadBlock, Reset, Clock, Validade, Dado_3, Valid_3, Tag_3, Dado_2, Valid_2, Tag_2, Dado_3_2, Valid_1, Tag_1, Dado_0, Valid_0, Tag_0
  Conjunto_teste conjunto_teste_19 ();  // open: Tag_in, Offset, LoadBlock, Reset, Clock, Validade, Dado_3, Valid_3, Tag_3, Dado_2, Valid_2, Tag_2, Dado_3_2, Valid_1, Tag_1, Dado_0, Valid_0, Tag_0
  Conjunto_teste conjunto_teste_20 ();  // open: Tag_in, Offset, LoadBlock, Reset, Clock, Validade, Dado_3, Valid_3, Tag_3, Dado_2, Valid_2, Tag_2, Dado_3_2, Valid_1, Tag_1, Dado_0, Valid_0, Tag_0
  Conjunto_teste conjunto_teste_21 ();  // open: Tag_in, Offset, LoadBlock, Reset, Clock, Validade, Dado_3, Valid_3, Tag_3, Dado_2, Valid_2, Tag_2, Dado_3_2, Valid_1, Tag_1, Dado_0, Valid_0, Tag_0
  Conjunto_teste conjunto_teste_22 ();  // open: Tag_in, Offset, LoadBlock, Reset, Clock, Validade, Dado_3, Valid_3, Tag_3, Dado_2, Valid_2, Tag_2, Dado_3_2, Valid_1, Tag_1, Dado_0, Valid_0, Tag_0
  Conjunto_teste conjunto_teste_23 ();  // open: Tag_in, Offset, LoadBlock, Reset, Clock, Validade, Dado_3, Valid_3, Tag_3, Dado_2, Valid_2, Tag_2, Dado_3_2, Valid_1, Tag_1, Dado_0, Valid_0, Tag_0
  Conjunto_teste conjunto_teste_24 ();  // open: Tag_in, Offset, LoadBlock, Reset, Clock, Validade, Dado_3, Valid_3, Tag_3, Dado_2, Valid_2, Tag_2, Dado_3_2, Valid_1, Tag_1, Dado_0, Valid_0, Tag_0
  Conjunto_teste conjunto_teste_25 ();  // open: Tag_in, Offset, LoadBlock, Reset, Clock, Validade, Dado_3, Valid_3, Tag_3, Dado_2, Valid_2, Tag_2, Dado_3_2, Valid_1, Tag_1, Dado_0, Valid_0, Tag_0
  Conjunto_teste conjunto_teste_26 ();  // open: Tag_in, Offset, LoadBlock, Reset, Clock, Validade, Dado_3, Valid_3, Tag_3, Dado_2, Valid_2, Tag_2, Dado_3_2, Valid_1, Tag_1, Dado_0, Valid_0, Tag_0
  Conjunto_teste conjunto_teste_27 ();  // open: Tag_in, Offset, LoadBlock, Reset, Clock, Validade, Dado_3, Valid_3, Tag_3, Dado_2, Valid_2, Tag_2, Dado_3_2, Valid_1, Tag_1, Dado_0, Valid_0, Tag_0
  Conjunto_teste conjunto_teste_28 ();  // open: Tag_in, Offset, LoadBlock, Reset, Clock, Validade, Dado_3, Valid_3, Tag_3, Dado_2, Valid_2, Tag_2, Dado_3_2, Valid_1, Tag_1, Dado_0, Valid_0, Tag_0
  Conjunto_teste conjunto_teste_29 ();  // open: Tag_in, Offset, LoadBlock, Reset, Clock, Validade, Dado_3, Valid_3, Tag_3, Dado_2, Valid_2, Tag_2, Dado_3_2, Valid_1, Tag_1, Dado_0, Valid_0, Tag_0
  Conjunto_teste conjunto_teste_30 ();  // open: Tag_in, Offset, LoadBlock, Reset, Clock, Validade, Dado_3, Valid_3, Tag_3, Dado_2, Valid_2, Tag_2, Dado_3_2, Valid_1, Tag_1, Dado_0, Valid_0, Tag_0
  Conjunto_teste conjunto_teste_31 ();  // open: Tag_in, Offset, LoadBlock, Reset, Clock, Validade, Dado_3, Valid_3, Tag_3, Dado_2, Valid_2, Tag_2, Dado_3_2, Valid_1, Tag_1, Dado_0, Valid_0, Tag_0
  Conjunto_teste conjunto_teste_32 ();  // open: Tag_in, Offset, LoadBlock, Reset, Clock, Validade, Dado_3, Valid_3, Tag_3, Dado_2, Valid_2, Tag_2, Dado_3_2, Valid_1, Tag_1, Dado_0, Valid_0, Tag_0
  Conjunto_teste conjunto_teste_33 ();  // open: Tag_in, Offset, LoadBlock, Reset, Clock, Validade, Dado_3, Valid_3, Tag_3, Dado_2, Valid_2, Tag_2, Dado_3_2, Valid_1, Tag_1, Dado_0, Valid_0, Tag_0
  Conjunto_teste conjunto_teste_34 ();  // open: Tag_in, Offset, LoadBlock, Reset, Clock, Validade, Dado_3, Valid_3, Tag_3, Dado_2, Valid_2, Tag_2, Dado_3_2, Valid_1, Tag_1, Dado_0, Valid_0, Tag_0
  Conjunto_teste conjunto_teste_35 ();  // open: Tag_in, Offset, LoadBlock, Reset, Clock, Validade, Dado_3, Valid_3, Tag_3, Dado_2, Valid_2, Tag_2, Dado_3_2, Valid_1, Tag_1, Dado_0, Valid_0, Tag_0
  Conjunto_teste conjunto_teste_36 ();  // open: Tag_in, Offset, LoadBlock, Reset, Clock, Validade, Dado_3, Valid_3, Tag_3, Dado_2, Valid_2, Tag_2, Dado_3_2, Valid_1, Tag_1, Dado_0, Valid_0, Tag_0
  Conjunto_teste conjunto_teste_37 ();  // open: Tag_in, Offset, LoadBlock, Reset, Clock, Validade, Dado_3, Valid_3, Tag_3, Dado_2, Valid_2, Tag_2, Dado_3_2, Valid_1, Tag_1, Dado_0, Valid_0, Tag_0
  Conjunto_teste conjunto_teste_38 ();  // open: Tag_in, Offset, LoadBlock, Reset, Clock, Validade, Dado_3, Valid_3, Tag_3, Dado_2, Valid_2, Tag_2, Dado_3_2, Valid_1, Tag_1, Dado_0, Valid_0, Tag_0
  Conjunto_teste conjunto_teste_39 ();  // open: Tag_in, Offset, LoadBlock, Reset, Clock, Validade, Dado_3, Valid_3, Tag_3, Dado_2, Valid_2, Tag_2, Dado_3_2, Valid_1, Tag_1, Dado_0, Valid_0, Tag_0
  Conjunto_teste conjunto_teste_40 ();  // open: Tag_in, Offset, LoadBlock, Reset, Clock, Validade, Dado_3, Valid_3, Tag_3, Dado_2, Valid_2, Tag_2, Dado_3_2, Valid_1, Tag_1, Dado_0, Valid_0, Tag_0
  Conjunto_teste conjunto_teste_41 ();  // open: Tag_in, Offset, LoadBlock, Reset, Clock, Validade, Dado_3, Valid_3, Tag_3, Dado_2, Valid_2, Tag_2, Dado_3_2, Valid_1, Tag_1, Dado_0, Valid_0, Tag_0
  Conjunto_teste conjunto_teste_42 ();  // open: Tag_in, Offset, LoadBlock, Reset, Clock, Validade, Dado_3, Valid_3, Tag_3, Dado_2, Valid_2, Tag_2, Dado_3_2, Valid_1, Tag_1, Dado_0, Valid_0, Tag_0
  Conjunto_teste conjunto_teste_43 ();  // open: Tag_in, Offset, LoadBlock, Reset, Clock, Validade, Dado_3, Valid_3, Tag_3, Dado_2, Valid_2, Tag_2, Dado_3_2, Valid_1, Tag_1, Dado_0, Valid_0, Tag_0
  Conjunto_teste conjunto_teste_44 ();  // open: Tag_in, Offset, LoadBlock, Reset, Clock, Validade, Dado_3, Valid_3, Tag_3, Dado_2, Valid_2, Tag_2, Dado_3_2, Valid_1, Tag_1, Dado_0, Valid_0, Tag_0
  Conjunto_teste conjunto_teste_45 ();  // open: Tag_in, Offset, LoadBlock, Reset, Clock, Validade, Dado_3, Valid_3, Tag_3, Dado_2, Valid_2, Tag_2, Dado_3_2, Valid_1, Tag_1, Dado_0, Valid_0, Tag_0
  Conjunto_teste conjunto_teste_46 ();  // open: Tag_in, Offset, LoadBlock, Reset, Clock, Validade, Dado_3, Valid_3, Tag_3, Dado_2, Valid_2, Tag_2, Dado_3_2, Valid_1, Tag_1, Dado_0, Valid_0, Tag_0
  Conjunto_teste conjunto_teste_47 ();  // open: Tag_in, Offset, LoadBlock, Reset, Clock, Validade, Dado_3, Valid_3, Tag_3, Dado_2, Valid_2, Tag_2, Dado_3_2, Valid_1, Tag_1, Dado_0, Valid_0, Tag_0
  Conjunto_teste conjunto_teste_48 ();  // open: Tag_in, Offset, LoadBlock, Reset, Clock, Validade, Dado_3, Valid_3, Tag_3, Dado_2, Valid_2, Tag_2, Dado_3_2, Valid_1, Tag_1, Dado_0, Valid_0, Tag_0
  Conjunto_teste conjunto_teste_49 ();  // open: Tag_in, Offset, LoadBlock, Reset, Clock, Validade, Dado_3, Valid_3, Tag_3, Dado_2, Valid_2, Tag_2, Dado_3_2, Valid_1, Tag_1, Dado_0, Valid_0, Tag_0
  Conjunto_teste conjunto_teste_50 ();  // open: Tag_in, Offset, LoadBlock, Reset, Clock, Validade, Dado_3, Valid_3, Tag_3, Dado_2, Valid_2, Tag_2, Dado_3_2, Valid_1, Tag_1, Dado_0, Valid_0, Tag_0
  Conjunto_teste conjunto_teste_51 ();  // open: Tag_in, Offset, LoadBlock, Reset, Clock, Validade, Dado_3, Valid_3, Tag_3, Dado_2, Valid_2, Tag_2, Dado_3_2, Valid_1, Tag_1, Dado_0, Valid_0, Tag_0
  Conjunto_teste conjunto_teste_52 ();  // open: Tag_in, Offset, LoadBlock, Reset, Clock, Validade, Dado_3, Valid_3, Tag_3, Dado_2, Valid_2, Tag_2, Dado_3_2, Valid_1, Tag_1, Dado_0, Valid_0, Tag_0
  Conjunto_teste conjunto_teste_53 ();  // open: Tag_in, Offset, LoadBlock, Reset, Clock, Validade, Dado_3, Valid_3, Tag_3, Dado_2, Valid_2, Tag_2, Dado_3_2, Valid_1, Tag_1, Dado_0, Valid_0, Tag_0
  Conjunto_teste conjunto_teste_54 ();  // open: Tag_in, Offset, LoadBlock, Reset, Clock, Validade, Dado_3, Valid_3, Tag_3, Dado_2, Valid_2, Tag_2, Dado_3_2, Valid_1, Tag_1, Dado_0, Valid_0, Tag_0
  Conjunto_teste conjunto_teste_55 ();  // open: Tag_in, Offset, LoadBlock, Reset, Clock, Validade, Dado_3, Valid_3, Tag_3, Dado_2, Valid_2, Tag_2, Dado_3_2, Valid_1, Tag_1, Dado_0, Valid_0, Tag_0
  Conjunto_teste conjunto_teste_56 ();  // open: Tag_in, Offset, LoadBlock, Reset, Clock, Validade, Dado_3, Valid_3, Tag_3, Dado_2, Valid_2, Tag_2, Dado_3_2, Valid_1, Tag_1, Dado_0, Valid_0, Tag_0
  Conjunto_teste conjunto_teste_57 ();  // open: Tag_in, Offset, LoadBlock, Reset, Clock, Validade, Dado_3, Valid_3, Tag_3, Dado_2, Valid_2, Tag_2, Dado_3_2, Valid_1, Tag_1, Dado_0, Valid_0, Tag_0
  Conjunto_teste conjunto_teste_58 ();  // open: Tag_in, Offset, LoadBlock, Reset, Clock, Validade, Dado_3, Valid_3, Tag_3, Dado_2, Valid_2, Tag_2, Dado_3_2, Valid_1, Tag_1, Dado_0, Valid_0, Tag_0
  Conjunto_teste conjunto_teste_59 ();  // open: Tag_in, Offset, LoadBlock, Reset, Clock, Validade, Dado_3, Valid_3, Tag_3, Dado_2, Valid_2, Tag_2, Dado_3_2, Valid_1, Tag_1, Dado_0, Valid_0, Tag_0
  Conjunto_teste conjunto_teste_60 ();  // open: Tag_in, Offset, LoadBlock, Reset, Clock, Validade, Dado_3, Valid_3, Tag_3, Dado_2, Valid_2, Tag_2, Dado_3_2, Valid_1, Tag_1, Dado_0, Valid_0, Tag_0
  Conjunto_teste conjunto_teste_61 ();  // open: Tag_in, Offset, LoadBlock, Reset, Clock, Validade, Dado_3, Valid_3, Tag_3, Dado_2, Valid_2, Tag_2, Dado_3_2, Valid_1, Tag_1, Dado_0, Valid_0, Tag_0
  Conjunto_teste conjunto_teste_62 ();  // open: Tag_in, Offset, LoadBlock, Reset, Clock, Validade, Dado_3, Valid_3, Tag_3, Dado_2, Valid_2, Tag_2, Dado_3_2, Valid_1, Tag_1, Dado_0, Valid_0, Tag_0
  Conjunto_teste conjunto_teste_63 ();  // open: Tag_in, Offset, LoadBlock, Reset, Clock, Validade, Dado_3, Valid_3, Tag_3, Dado_2, Valid_2, Tag_2, Dado_3_2, Valid_1, Tag_1, Dado_0, Valid_0, Tag_0
  Conjunto_teste conjunto_teste_64 ();  // open: Tag_in, Offset, LoadBlock, Reset, Clock, Validade, Dado_3, Valid_3, Tag_3, Dado_2, Valid_2, Tag_2, Dado_3_2, Valid_1, Tag_1, Dado_0, Valid_0, Tag_0
  Mux_64_1 mux_64_1_1 (
    .Index(\Endereço [9:4]), .in_2(conjunto_teste_1_tag_3));  // open: in_3, in_4, in_5, in_6, in_7, in_8, in_9, in_10, in_11, in_12, in_13, in_14, in_15, in_16, in_17, in_18, in_19, in_20, in_21, in_22, in_23, in_24, in_25, in_26, in_27, in_28, in_29, in_30, in_31, in_32, in_33, in_34, in_35, in_36, in_37, in_38, in_39, in_40, in_41, in_42, in_43, in_44, in_45, in_46, in_47, in_48, in_49, in_50, in_51, in_52, in_53, in_54, in_55, in_56, in_57, in_58, in_59, in_60, in_61, in_62, in_63, in_64, in_65, Tag
  Mux_64_1 mux_64_1_2 (.Index(\Endereço [9:4]));  // open: in_2, in_3, in_4, in_5, in_6, in_7, in_8, in_9, in_10, in_11, in_12, in_13, in_14, in_15, in_16, in_17, in_18, in_19, in_20, in_21, in_22, in_23, in_24, in_25, in_26, in_27, in_28, in_29, in_30, in_31, in_32, in_33, in_34, in_35, in_36, in_37, in_38, in_39, in_40, in_41, in_42, in_43, in_44, in_45, in_46, in_47, in_48, in_49, in_50, in_51, in_52, in_53, in_54, in_55, in_56, in_57, in_58, in_59, in_60, in_61, in_62, in_63, in_64, in_65, Tag
endmodule

module Dec6_1 (
  input  [5:0] Index,
  output out_2,
  output out_3,
  output out_4,
  output out_5,
  output out_6,
  output out_7,
  output out_8,
  output out_9,
  output out_10,
  output out_11,
  output out_12,
  output out_13,
  output out_14,
  output out_15,
  output out_16,
  output out_17,
  output out_18,
  output out_19,
  output out_20,
  output out_21,
  output out_22,
  output out_23,
  output out_24,
  output out_25,
  output out_26,
  output out_27,
  output out_28,
  output out_29,
  output out_30,
  output out_31,
  output out_32,
  output out_33,
  output out_34,
  output out_35,
  output out_36,
  output out_37,
  output out_38,
  output out_39,
  output out_40,
  output out_41,
  output out_42,
  output out_43,
  output out_44,
  output out_45,
  output out_46,
  output out_47,
  output out_48,
  output out_49,
  output out_50,
  output out_51,
  output out_52,
  output out_53,
  output out_54,
  output out_55,
  output out_56,
  output out_57,
  output out_58,
  output out_59,
  output out_60,
  output out_61,
  output out_62,
  output out_63,
  output out_64,
  output out_65
);

  wire decoder_1_out0, decoder_2_out0, not_1_out, not_2_out, not_3_out, not_4_out, not_5_out;
  wire [4:0] and_1_out, and_6_out;

  not not_1 (not_1_out, Index[5]);
  not not_2 (not_2_out, Index[5]);
  not not_3 (not_3_out, Index[5]);
  not not_4 (not_4_out, Index[5]);
  not not_5 (not_5_out, Index[5]);
  and and_1 (and_1_out[0], not_1_out, Index[0]);
  and and_2 (and_1_out[1], not_2_out, Index[1]);
  and and_3 (and_1_out[2], not_3_out, Index[2]);
  and and_4 (and_1_out[3], not_4_out, Index[3]);
  and and_5 (and_1_out[4], not_5_out, Index[4]);
  and and_6 (and_6_out[0], Index[5], Index[0]);
  and and_7 (and_6_out[1], Index[5], Index[1]);
  and and_8 (and_6_out[2], Index[5], Index[2]);
  and and_9 (and_6_out[3], Index[5], Index[3]);
  and and_10 (and_6_out[4], Index[5], Index[4]);
  Decoder #(.select(5), .enable("false")) decoder_1 (
    .out0(decoder_1_out0), .out1(out_3), .out2(out_4), .out3(out_5), .out4(out_6), .out5(out_7),
    .out6(out_8), .out7(out_9), .out8(out_10), .out9(out_11), .out10(out_12), .out11(out_13), .out12(out_14),
    .out13(out_15), .out14(out_16), .out15(out_17), .out16(out_18), .out17(out_19), .out18(out_20),
    .out19(out_21), .out20(out_22), .out21(out_23), .out22(out_24), .out23(out_25), .out24(out_26),
    .out25(out_27), .out26(out_28), .out27(out_29), .out28(out_30), .out29(out_31), .out30(out_32),
    .out31(out_33), .sel(and_1_out));
  Decoder #(.select(5), .enable("false")) decoder_2 (
    .out0(decoder_2_out0), .out1(out_35), .out2(out_36), .out3(out_37), .out4(out_38), .out5(out_39),
    .out6(out_40), .out7(out_41), .out8(out_42), .out9(out_43), .out10(out_44), .out11(out_45),
    .out12(out_46), .out13(out_47), .out14(out_48), .out15(out_49), .out16(out_50), .out17(out_51),
    .out18(out_52), .out19(out_53), .out20(out_54), .out21(out_55), .out22(out_56), .out23(out_57),
    .out24(out_58), .out25(out_59), .out26(out_60), .out27(out_61), .out28(out_62), .out29(out_63),
    .out30(out_64), .out31(out_65), .sel(and_6_out));
  and and_11 (out_2, not_1_out, decoder_1_out0);
  and and_12 (out_34, Index[5], decoder_2_out0);
endmodule

module Conjunto_teste (
  input  [21:0] Tag_in,
  input  [3:0] Offset,
  input  LoadBlock,
  input  Reset,
  input  Clock,
  input  Validade,
  output [7:0] Dado_3,
  output Valid_3,
  output [21:0] Tag_3,
  output [7:0] Dado_2,
  output Valid_2,
  output [21:0] Tag_2,
  output [7:0] Dado_3_2,
  output Valid_1,
  output [21:0] Tag_1,
  output [7:0] Dado_0,
  output Valid_0,
  output [21:0] Tag_0
);

  // Linha_bloco linha_bloco_1: pin names not known; wires that end beside it: Tag_in, Validade, Clock, Tag_0, Reset, Valid_0, LoadBlock, Dado_0, Offset
  // Linha_bloco linha_bloco_2: pin names not known; wires that end beside it: Tag_in, Validade, Clock, Tag_1, Reset, Valid_1, LoadBlock, Dado_3_2, Offset
  // Linha_bloco linha_bloco_3: pin names not known; wires that end beside it: Tag_in, Validade, Clock, Tag_2, Reset, Valid_2, LoadBlock, Dado_2, Offset
  // Linha_bloco linha_bloco_4: pin names not known; wires that end beside it: Tag_in, Validade, Clock, Tag_3, Reset, Valid_3, LoadBlock, Dado_3, Offset

  // Notes on the sheet:
  //   fazer alguma coisa para selecionar bloco para substituir
  //   Essa parte é para quando acontece miss
endmodule

module Mux_64_1 (
  input  [5:0] Index,
  input  [21:0] in_2,
  input  [21:0] in_3,
  input  [21:0] in_4,
  input  [21:0] in_5,
  input  [21:0] in_6,
  input  [21:0] in_7,
  input  [21:0] in_8,
  input  [21:0] in_9,
  input  [21:0] in_10,
  input  [21:0] in_11,
  input  [21:0] in_12,
  input  [21:0] in_13,
  input  [21:0] in_14,
  input  [21:0] in_15,
  input  [21:0] in_16,
  input  [21:0] in_17,
  input  [21:0] in_18,
  input  [21:0] in_19,
  input  [21:0] in_20,
  input  [21:0] in_21,
  input  [21:0] in_22,
  input  [21:0] in_23,
  input  [21:0] in_24,
  input  [21:0] in_25,
  input  [21:0] in_26,
  input  [21:0] in_27,
  input  [21:0] in_28,
  input  [21:0] in_29,
  input  [21:0] in_30,
  input  [21:0] in_31,
  input  [21:0] in_32,
  input  [21:0] in_33,
  input  [21:0] in_34,
  input  [21:0] in_35,
  input  [21:0] in_36,
  input  [21:0] in_37,
  input  [21:0] in_38,
  input  [21:0] in_39,
  input  [21:0] in_40,
  input  [21:0] in_41,
  input  [21:0] in_42,
  input  [21:0] in_43,
  input  [21:0] in_44,
  input  [21:0] in_45,
  input  [21:0] in_46,
  input  [21:0] in_47,
  input  [21:0] in_48,
  input  [21:0] in_49,
  input  [21:0] in_50,
  input  [21:0] in_51,
  input  [21:0] in_52,
  input  [21:0] in_53,
  input  [21:0] in_54,
  input  [21:0] in_55,
  input  [21:0] in_56,
  input  [21:0] in_57,
  input  [21:0] in_58,
  input  [21:0] in_59,
  input  [21:0] in_60,
  input  [21:0] in_61,
  input  [21:0] in_62,
  input  [21:0] in_63,
  input  [21:0] in_64,
  input  [21:0] in_65,
  output [21:0] Tag
);

  wire not_1_out, not_2_out, not_3_out, not_4_out, not_5_out;
  wire [4:0] and_1_out, and_6_out;
  wire [21:0] multiplexer_1_out, multiplexer_2_out;

  not not_1 (not_1_out, Index[5]);
  not not_2 (not_2_out, Index[5]);
  not not_3 (not_3_out, Index[5]);
  not not_4 (not_4_out, Index[5]);
  not not_5 (not_5_out, Index[5]);
  and and_1 (and_1_out[0], not_1_out, Index[0]);
  and and_2 (and_1_out[1], not_2_out, Index[1]);
  and and_3 (and_1_out[2], not_3_out, Index[2]);
  and and_4 (and_1_out[3], not_4_out, Index[3]);
  and and_5 (and_1_out[4], not_5_out, Index[4]);
  and and_6 (and_6_out[0], Index[5], Index[0]);
  and and_7 (and_6_out[1], Index[5], Index[1]);
  and and_8 (and_6_out[2], Index[5], Index[2]);
  and and_9 (and_6_out[3], Index[5], Index[3]);
  and and_10 (and_6_out[4], Index[5], Index[4]);
  Multiplexer #(.select(5), .width(22), .enable("false")) multiplexer_1 (
    .in0(in_2), .in1(in_3), .in2(in_4), .in3(in_5), .in4(in_6), .in5(in_7), .in6(in_8), .in7(in_9),
    .in8(in_10), .in9(in_11), .in10(in_12), .in11(in_13), .in12(in_14), .in13(in_15), .in14(in_16),
    .in15(in_17), .in16(in_18), .in17(in_19), .in18(in_20), .in19(in_21), .in20(in_22), .in21(in_23),
    .in22(in_24), .in23(in_25), .in24(in_26), .in25(in_27), .in26(in_28), .in27(in_29), .in28(in_30),
    .in29(in_31), .in30(in_32), .in31(in_33), .out(multiplexer_1_out), .sel(and_1_out));
  Multiplexer #(.select(5), .width(22), .enable("false")) multiplexer_2 (
    .in0(in_34), .in1(in_35), .in2(in_36), .in3(in_37), .in4(in_38), .in5(in_39), .in6(in_40), .in7(in_41),
    .in8(in_42), .in9(in_43), .in10(in_44), .in11(in_45), .in12(in_46), .in13(in_47), .in14(in_48),
    .in15(in_49), .in16(in_50), .in17(in_51), .in18(in_52), .in19(in_53), .in20(in_54), .in21(in_55),
    .in22(in_56), .in23(in_57), .in24(in_58), .in25(in_59), .in26(in_60), .in27(in_61), .in28(in_62),
    .in29(in_63), .in30(in_64), .in31(in_65), .out(multiplexer_2_out), .sel(and_6_out));
  Multiplexer #(.width(22), .enable("false")) multiplexer_3 (
    .in0(multiplexer_1_out), .in1(multiplexer_2_out), .out(Tag), .sel(Index[5]));
endmodule
